# Fritzing sketch slaveSetup (saved by Fritzing 0.9.3b)

parts:
  Part2 = XBee Explorer Regulated
  Part3 = LSM303C (6 DOF)
  U1 = LIPO-2000mAh [package=lipo-2000]
  J1 = Power Jack [package=power_jack_pth_lock]
  Part4 = Arduino Uno (Rev3)
  Part5 = Arduino Uno (Rev3)
  Part6 = Arduino Motor Shield
  M1 = DC Motor
  M2 = DC Motor
  M3 = DC Motor
  M4 = DC Motor
  LCD1 = LCD screen
  hc-sr1 = hc-sr04
  U2 = LIPO-2000mAh [package=lipo-2000]
  J2 = Infrared Proximity Sensor

nets (from the schematic view):
  N1: Part2.DIN, Part4.D2
  N2: Part2.DOUT, Part4.D3_PWM
  5V: Part2.5V, Part4.5V
  GND: Part2.GND, Part4.GND
  N3: Part3.SDA/SDI/SDO, Part4.A4/SDA
  N4: Part3.SCL/SCLK, Part4.A5/SCL
  VCC: Part3.VCC, Part4.3V3
  N5: U1.+, J1.GND
  N6: U1.-, J1.GNDBREAK, J1.PWR, Part4.VIN
  N7: Part4.D1/TX, Part5.D1/TX
  GND_2: Part5.GND, J2.GND
  GND_3: Part6.GND, LCD1.DB6, hc-sr1.GND, U2.-
  N8: Part6.VIN, U2.+
  N9: Part6.OUT3, M3.pin_2, M4.pin_2
  N10: Part6.OUT4, M3.pin_1, M4.pin_1
  N11: Part6.OUT1, M1.pin_1, M2.pin_1
  N12: Part6.OUT2, M1.pin_2, M2.pin_2
  5V_2: Part6.5V, LCD1.DB4, J2.Vcc
  N13: Part6.A2, J2.Vout
  N14: Part6.D3, LCD1.LED-
  N15: Part6.D7, hc-sr1.Echo
  N16: Part6.D8, hc-sr1.Trig
  N17: LCD1.DB5, hc-sr1.VCC

notes:
  Batteries must be 7.4V
